# Fritzing sketch Diagrama_Electrico_TFG (saved by Fritzing 1.0.6)

parts:
  Part1 = Arduino Uno (Rev3)
  A1 = Raspberry Pi 5  # not connected
  M1 = RioRand LM2596
  KY-1 = Keyes Hall Effect Sensor [package=THT]
  M2 = BME280
  M3 = 1 chan 5v relay module
  JACK1 = 2.1mm Barrel Jack with Terminal Block
  LED2 = LEDs [package=led10mm]
  R1 = Resistor [tolerance=±5% power=0.25W resistance=47 package=THT]
  USBTTL1 = Micro USB B Plug  # not connected
  F1 = Fan - Ventilador [package=THT]
  USBTTL3 = USB A Plug
  LED1 = LEDs [package=led10mm]
  USBTTL2 = USB A Plug
  J1 = Basic Servo
  J2 = female pin header, 6 pins [form="♀ (female)"]
  J3 = female pin header, 6 pins [form="♀ (female)"]

nets:
  N1: Part1.A4/SDA, M2.SDA
  N2: Part1.A5/SCL, M2.SCL
  N3: Part1.D8, R1.Pin_1
  N4: Part1.D9_PWM, J1.pulse
  N5: Part1.D11_PWM/MOSI, KY-1.signal
  N6: Part1.D12/MISO, M3.pin_3
  N7: Part1.GND, M1.Pin_4, KY-1.ground, M3.pin_2, LED2.A, LED1.A
  N8: Part1.VIN, M1.Pin_3, KY-1.power, M3.pin_1
  N9: M1.Pin_1, M3.pin_6, JACK1.POS
  N10: M1.Pin_2, JACK1.NEG, F1.GND
  VIN: M2.VIN, J1.vcc
  GND: M2.GND, J1.gnd
  N11: M3.pin_5, F1.5V
  N12: LED2.C, R1.Pin_0, LED1.C
  N13: USBTTL3.usb, USBTTL2.usb
  N14: J2.pin1, J3.pin1
  N15: J2.pin2, J3.pin2
  N16: J2.pin3, J3.pin3
  N17: J2.pin4, J3.pin4
  N18: J2.pin5, J3.pin5
  N19: J2.pin6, J3.pin6

notes:
  Fuente de Alimentacion 12V
  Fuente de Alimentacion 5V

custom parts:
  Raspberry Pi 5: The RPi5, a faster version of the awesome Raspberry Pi4B ARM Board with 40 pin gpio.
  Keyes Hall Effect Sensor: Keyes Magnetic Hall Effect Sensor Module for Arduino. Working voltage: 4.5V-25V.
  BME280: Temperature Humidity Barometric presure Sensor
  1 chan 5v relay module: 1 Channel 5V Relay Module Board Shield with Optocoupler Support High and Low Level Trigger for Arduino.
  Fan - Ventilador: Ventilador de 2 pines, se encuentra comunmente en computadoras de escritorio
